// Logisim project No-ALU Game.circ as structural Verilog: 1 circuit, main circuit main
module main (
  input  in_1
);

  wire clock_1_out, clock_2_out;
  wire [3:0] demultiplexer_1_out0, demultiplexer_1_out1, demultiplexer_1_out2, demultiplexer_1_out3,
       demultiplexer_1_out4, demultiplexer_1_out5, demultiplexer_1_out6, demultiplexer_1_out7,
       demultiplexer_1_out8, demultiplexer_1_out9, demultiplexer_1_out10, demultiplexer_1_out11,
       demultiplexer_1_out12, demultiplexer_1_out13, demultiplexer_1_out14, demultiplexer_1_out15;
  wire [4:0] counter_1_q;
  wire [11:5] pull_resistor_3_node;
  wire [15:0] ram_1_dout;

  Counter #(.max('h1f), .trigger("falling"), .width(5)) counter_1 (
    .clr(in_1), .up(1'b1), .clk(clock_1_out), .Q(counter_1_q));  // open: load, count, D, carry
  Clock clock_1 (.out(clock_1_out));
  Pull_Resistor pull_resistor_1 (.node(pull_resistor_3_node[8:5]));
  Pull_Resistor pull_resistor_2 (.node(pull_resistor_3_node[9]));
  Pull_Resistor pull_resistor_3 (.node(pull_resistor_3_node[10]));
  RAM #(.addrWidth(12), .dataWidth(16), .\type ("nonvolatile")) ram_1 (
    .addr({pull_resistor_3_node, counter_1_q}), .oe(1'b1), .clk(clock_2_out),
    .dout({ram_1_dout[15:13], pull_resistor_3_node[9:5], ram_1_dout[7:0]}));  // open: we, din
  Clock clock_2 (.out(clock_2_out));
  Pull_Resistor pull_resistor_4 (.node(pull_resistor_3_node[11]));
  DotMatrix #(.matrixcols(16), .matrixrows(4), .persist(2)) dotmatrix_1 (
    .col0(demultiplexer_1_out0), .col1(demultiplexer_1_out1), .col2(demultiplexer_1_out2),
    .col3(demultiplexer_1_out3), .col4(demultiplexer_1_out4), .col5(demultiplexer_1_out5),
    .col6(demultiplexer_1_out6), .col7(demultiplexer_1_out7), .col8(demultiplexer_1_out8),
    .col9(demultiplexer_1_out9), .col10(demultiplexer_1_out10), .col11(demultiplexer_1_out11),
    .col12(demultiplexer_1_out12), .col13(demultiplexer_1_out13), .col14(demultiplexer_1_out14),
    .col15(demultiplexer_1_out15));
  // Switch JUMP: pin names not known; wires that end beside it: ram_1_dout[13], pull_resistor_3_node[10]
  // Switch R: pin names not known; wires that end beside it: ram_1_dout[14], pull_resistor_3_node[11]
  Demultiplexer #(.select(4), .width(4)) demultiplexer_1 (
    .out0(demultiplexer_1_out0), .out1(demultiplexer_1_out1), .out2(demultiplexer_1_out2),
    .out3(demultiplexer_1_out3), .out4(demultiplexer_1_out4), .out5(demultiplexer_1_out5),
    .out6(demultiplexer_1_out6), .out7(demultiplexer_1_out7), .out8(demultiplexer_1_out8),
    .out9(demultiplexer_1_out9), .out10(demultiplexer_1_out10), .out11(demultiplexer_1_out11),
    .out12(demultiplexer_1_out12), .out13(demultiplexer_1_out13), .out14(demultiplexer_1_out14),
    .out15(demultiplexer_1_out15), .in(ram_1_dout[7:4]), .sel(ram_1_dout[3:0]));
  // Buzzer buzzer_1: pin names not known; wires that end beside it: 14'h1fff, ram_1_dout[15], {7{1'b1}}
endmodule
